# Fritzing sketch Voicecontrolled bot (saved by Fritzing 0.8.7b)

parts:
  Part2 = Arduino Uno (Rev3)
  J1 = Basic Servo
  M2 = DC Motor
  Part3 = Bluetooth HC-05 Macho
  Part5 = Adafruit Motor/Stepper/Servo Shield [part_number="Adafruit #1438"]
  M3 = DC Motor
  Part6 = FC-03 [chip_label=FC-03]

nets:
  N1: Part2.D11_PWM/MOSI, Part6.pin_4
  N2: Part2.D0/RX, Part3.TXD
  N3: Part2.D1/TX, Part3.RXD
  5V: Part2.5V, Part3.VCC, Part6.pin_1
  GND: Part2.GND, Part3.GND, Part6.pin_2
  N4: J1.gnd, Part5.D10
  VCC: J1.vcc, Part5.+5V
  N5: J1.pulse, Part5.GND
  N6: M2.pin_1, Part5.M1B
  N7: M2.pin_2, Part5.M1A
  N8: Part5.M2A, M3.pin_1

notes:
  LM93 Speed Sensor
  HC 05 Bluetooth
  Servo Shield
  Servo motor

custom parts:
  Adafruit Motor/Stepper/Servo Shield: The original Adafruit Motorshield kit is one of our most beloved kits, which is why we decided to make something even better. We have upgraded the shield kit to make the bestest, easiest way to drive DC and Stepper motors. This shield will make quick work of your next robotics project! We kept the ability to drive up to 4 DC motors or 2 stepper motors, but added many improvements: Instead of a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
  FC-03: FC-03, LM393 IR Speed Sensor Encoder
